# Fritzing sketch Untitled Sketch 2 (saved by Fritzing 0.9.3b)
circuit board: 8.46667cm x 5.64444cm
breadboards: 1

parts:
  LED1 = LED - 5mm [color="Red (633nm)" package="5 mm [THT]"]
  S2 = Round Pushbutton
  S3 = Round Pushbutton
  S4 = Round Pushbutton
  S5 = Round Pushbutton
  LED2 = smd LED [color="Red (633nm)" package="0603 [SMD]"]
  R1 = Resistor [tolerance=±5% resistance=220 package=THT]
  R2 = Resistor [tolerance=±5% resistance=220 package=THT]
  R3 = Resistor [tolerance=±5% resistance=220 package=THT]
  R4 = Resistor [tolerance=±5% resistance=220 package=THT]
  R5 = Resistor [tolerance=±5% resistance=220 package=THT]
  R6 = Resistor [tolerance=±5% resistance=220 package=THT]
  Part1 = Arduino Mega ADK (Rev3)
  Part2 = Arduino Ethernet Shield (Rev3)

nets:
  N1: LED1.cathode, S2.leg0, S3.leg0, S4.leg0, S5.leg0, LED2.cathode
  N2: LED1.anode, R6.Pin_0
  N3: S2.leg1, R2.Pin_1, Part1.D4_PWM
  N4: S3.leg1, R1.Pin_1, Part1.D5_PWM
  N5: S4.leg1, R3.Pin_1, Part1.D3_PWM
  N6: S5.leg1, R4.Pin_1, Part1.D2_PWM
  N7: LED2.anode, R5.Pin_0
  N8: R1.Pin_0, R2.Pin_0, R3.Pin_0, R4.Pin_0
  N9: R5.Pin_1, Part1.D8_PWM
  N10: R6.Pin_1, Part1.D9_PWM
  N11: Part1.D7_PWM, Part2.RESET
